# Fritzing sketch oreilly_light_control (saved by Fritzing 0.8.3b)
stripboards: 2

parts:
  Part2 = Arduino Pro Mini v13
  DC = Power plug
  U2 = RJ45 Jack [package=rj45-8]
  U3 = RJ45 Jack [package=rj45-8]
  IC1 = IC, DIP package, 8 pins [chip_label=OPTO]
  U4 = RJ45 Jack [package=rj45-8]
  S2 = Square Pushbutton
  S3 = Square Pushbutton
  LED2 = LED - 5mm [color="Green (565nm)" package="5 mm [THT]"]
  LED3 = LED - 5mm [color="Red (633nm)" package="5 mm [THT]"]
  LED4 = LED - 3mm [color="Red (633nm)" package="3 mm [THT]"]
  R2 = Resistor [tolerance=±5% resistance=190 package=THT]
  R3 = Resistor [tolerance=±5% resistance=190 package=THT]
  R4 = Resistor [tolerance=±5% resistance=220 package=THT]
  R5 = Resistor [tolerance=±5% resistance=220 package=THT]
  R6 = Resistor [tolerance=±5% resistance=220 package=THT]
  C2 = Electrolytic Capacitor [capacitance=10µF package="100 mil [THT, electrolytic]"]
  C3 = Electrolytic Capacitor [capacitance=1µF package="100 mil [THT, electrolytic]"]
  U5 = Voltage Regulator - 5V [package="TO220 [THT]"]

nets:
  GND: Part2.GND, DC.GND, U3.1, C2.-, C3.-, U5.GND
  N1: Part2.VCC, C3.+, U5.output_voltage
  N2: Part2.D8, R3.Pin_1
  N3: Part2.D7, R2.Pin_0
  N4: Part2.D6_PWM, U3.6
  N5: Part2.D5_PWM, U3.5
  N6: Part2.D4, U3.4
  N7: Part2.D3_PWM, U3.3
  N8: Part2.D2, U3.2
  N9: DC.VCC, C2.+, U5.input_voltage
  N10: U2.1, IC1.pin8
  N11: U2.2, IC1.pin7
  N12: U2.3, IC1.pin6
  N13: U2.4, IC1.pin5
  N14: IC1.pin1, IC1.pin3
  N15: IC1.pin2, R3.Pin_0
  N16: IC1.pin4, R2.Pin_1
  N17: U4.1, S2.leg0, S3.leg0, LED2.cathode, LED3.cathode, LED4.cathode
  N18: U4.2, R6.Pin_0
  N19: U4.3, LED2.anode
  N20: U4.4, R5.Pin_0
  N21: U4.5, LED3.anode
  N22: U4.6, R4.Pin_1
  N23: S2.leg1, R6.Pin_1
  N24: S3.leg1, R5.Pin_1
  N25: LED4.anode, R4.Pin_0
