# Fritzing sketch oreilly_light_control_2_final (saved by Fritzing 0.9.0b)
stripboards: 1

parts:
  U1 = Voltage Regulator - 5V [package="DPak [SMD]"]
  C1 = Electrolytic Capacitor [capacitance=10µF package="100 mil [THT, electrolytic]"]
  C2 = Electrolytic Capacitor [capacitance=10µF package="100 mil [THT, electrolytic]"]
  J1 = female pin header, 8 pins [form="♀ (female)"]
  LED-ON = LED - 5mm [color="Green (565nm)" package="5 mm [THT]"]
  LED-OFF = LED - 5mm [color="Red (635nm)" package="5 mm [THT]"]
  LED-PWR = LED - 3mm [color="Red (635nm)" current=10mA package="3 mm [THT]"]
  R1 = Resistor [tolerance=±5% resistance=1k package=THT]
  SWITCH-OFF = Pushbutton [package=THT]
  R2 = Resistor [tolerance=±5% resistance=1k package=THT]
  SWITCH-ON = Pushbutton [package=THT]
  R3 = Resistor [tolerance=±5% resistance=1k package=THT]
  Part1 = Arduino Pro Mini v13
  R4 = Resistor [tolerance=±5% resistance=180 package=THT]
  R5 = Resistor [tolerance=±5% resistance=180 package=THT]
  R6 = Resistor [tolerance=±5% resistance=1.5k package=THT]
  R7 = Resistor [tolerance=±5% resistance=1.5k package=THT]
  U4 = ACPL-824 [package="DIP (Dual Inline) [THT]"]
  R8 = Resistor [tolerance=±5% resistance=500 package=THT]
  R9 = Resistor [tolerance=±5% resistance=180 package=THT]
  R11 = Resistor [tolerance=±5% resistance=180 package=THT]
  U3 = ACPL-824 [package="DIP (Dual Inline) [THT]"]
  R12 = Resistor [tolerance=±5% resistance=390k package=THT]
  R14 = Resistor [tolerance=±5% resistance=390k package=THT]
  J3 = female pin header, 6 pins [form="♀ (female)"]
  J4 = female pin header, 6 pins [form="♀ (female)"]
  J2 = female pin header, 4 pins [form="♀ (female)"]

nets (from the schematic view):
  N1: U1.input_voltage, C2.+, J1.pin8
  GND: U1.GND, C1.-, C2.-, J1.pin1, Part1.GND, U4.IN_2b, U3.IN_1b, U3.IN_2b, R12.Pin_1, R14.Pin_1
  N2: U1.output_voltage, C1.+, Part1.VCC, R11.Pin_0, J4.pin1
  N3: J1.pin3, R6.Pin_0
  N4: J1.pin4, U3.Emitter_2
  N5: J1.pin5, R7.Pin_0
  N6: J1.pin6, U3.Emitter_1
  N7: LED-ON.cathode, J3.pin2
  N8: LED-ON.anode, LED-OFF.anode, LED-PWR.anode, SWITCH-OFF.leg1, SWITCH-ON.leg1, J3.pin1
  N9: LED-OFF.cathode, J3.pin4
  N10: LED-PWR.cathode, J3.pin6
  N11: R1.Pin_1, J4.pin6
  N12: SWITCH-OFF.leg0, J3.pin5
  N13: R2.Pin_0, R12.Pin_0, J4.pin3
  N14: R2.Pin_1, Part1.D2
  N15: SWITCH-ON.leg0, J3.pin3
  N16: R3.Pin_0, R14.Pin_0, J4.pin5
  N17: R3.Pin_1, Part1.D3_PWM
  N18: Part1.D8, R5.Pin_1
  N19: Part1.D7, R4.Pin_1
  N20: Part1.D5_PWM, J4.pin4
  N21: Part1.D1/RX, U4.Emitter_1
  N22: Part1.D0/TX, R9.Pin_0
  N23: R4.Pin_0, U3.IN_1a
  N24: R5.Pin_0, U3.IN_2a
  N25: R6.Pin_1, U3.Collector_1
  N26: R7.Pin_1, U3.Collector_2
  N27: U4.IN_1a, R8.Pin_1
  N28: U4.IN_1b, U4.Emitter_2, J2.pin2
  N29: U4.IN_2a, R9.Pin_1
  N30: U4.Collector_2, J2.pin1
  N31: U4.Collector_1, R11.Pin_1
  N32: R8.Pin_0, J2.pin3

custom parts:
  ACPL-824: The ACPL-824 is an AC-input dual channel full-pitch phototransistor optocoupler which contains four light emitting diode optically coupled to two separate phototransistor. I
